# Fritzing sketch ArduinoTIP120-MotorDriver (saved by Fritzing 0.9.2b)
breadboards: 1

parts:
  Part1 = Arduino Nano (Rev3.0)
  DC_MOTOR = DC Motor
  part = Rectifier Diode [part_number=1N4001 package="300 mil [THT]"]
  part_2 = Resistor [tolerance=±5% resistance=10k package=THT]
  9V-15V = Power plug
  TIP120 = npn-Powertransistor [package="TO220 [THT]"]
  10K_-_POT = Rotary Potentiometer (Small) [maximum_resistance=0.1MΩ package=THT]

nets:
  GND: Part1.GND, part.anode, 9V-15V.GND, TIP120.emitter, 10K_-_POT.leg1
  N1: Part1.D9, part_2.Pin_0
  VIN: Part1.VIN, DC_MOTOR.pin_1, 9V-15V.VCC
  N2: Part1.5V, 10K_-_POT.leg2
  N3: Part1.A0, 10K_-_POT.wiper
  N4: DC_MOTOR.pin_2, part.cathode, TIP120.collector
  N5: part_2.Pin_1, TIP120.base

notes:
  9V-15V
  TIP120
  DC MOTOR
